// Logisim project WhatTheHell.circ as structural Verilog: 2 circuits, main circuit main
module main (
  input  in_1
);

  wire and_4_out, C, comparator_1_eq, nand_1_out, nand_2_out, nand_3_out, not_2_out, not_3_out, or_1_out,
       or_2_out, verifier_1_d, xor_1_out, xor_4_out;
  wire [3:0] and_1_out;
  wire [6:0] and_3_out, and_5_out, demultiplexer_1_out0, demultiplexer_1_out1, demultiplexer_2_out1,
       demultiplexer_3_out1, multiplexer_1_out, multiplexer_2_out, multiplexer_3_out, verifier_1_o;
  wire [7:0] adder_1_out, adder_2_out, and_2_out, nor_1_out, not_1_out, xor_2_out, xor_3_out;

  Clock clock_1 (.out(C));
  Adder adder_1 (.a({8{1'b0}}), .b({8{1'b0}}), .out(adder_1_out));  // open: cin, cout
  Demultiplexer #(.width(7)) demultiplexer_1 (
    .out0(demultiplexer_1_out0), .out1(demultiplexer_1_out1), .in(7'b1101011), .sel(comparator_1_eq));
  Comparator comparator_1 (.a({8{1'b0}}), .b({8{1'b0}}), .eq(comparator_1_eq));  // open: gt, lt
  assign and_1_out = 4'b0000 & 4'b0000;  // AND_Gate and_1, 4 bits wide
  assign not_1_out = ~{8{1'b0}};  // NOT_Gate not_1, 8 bits wide
  assign nor_1_out = ~({8{1'b0}} | {8{1'b0}});  // NOR_Gate nor_1, 8 bits wide
  assign and_2_out = {8{1'b0}} & {8{1'b0}};  // AND_Gate and_2, 8 bits wide
  xor xor_1 (xor_1_out, adder_1_out[1], adder_1_out[2]);
  nand nand_1 (nand_1_out, and_1_out[0], and_1_out[2]);
  nand nand_2 (nand_2_out, and_1_out[1], and_1_out[3]);
  Adder adder_2 (.a({8{1'b0}}), .b(not_1_out), .out(adder_2_out));  // open: cin, cout
  assign and_3_out = demultiplexer_1_out0 & demultiplexer_1_out0;  // AND_Gate and_3, 7 bits wide
  Demultiplexer #(.width(7)) demultiplexer_2 (
    .out1(demultiplexer_2_out1), .in(7'b1110101), .sel(and_4_out));  // open: out0
  nand nand_3 (nand_3_out, adder_1_out[0], adder_1_out[3]);
  assign xor_2_out = adder_2_out ^ {8{1'b0}};  // XOR_Gate xor_2, 8 bits wide
  assign xor_3_out = {8{1'b0}} ^ and_2_out;  // XOR_Gate xor_3, 8 bits wide
  and and_4 (and_4_out, ~nand_3_out, xor_1_out, adder_1_out[5], not_2_out);  // AND_Gate
  not not_2 (not_2_out, or_1_out);
  or or_1 (or_1_out, adder_1_out[4], adder_1_out[1], adder_1_out[7]);
  or or_2 (or_2_out, nand_1_out, nand_2_out);
  xor xor_4 (xor_4_out, comparator_1_eq, nor_1_out[6]);
  Multiplexer #(.width(7)) multiplexer_1 (.in0({7{1'b0}}), .in1(7'b1000101), .out(multiplexer_1_out), .sel(or_2_out));
  Demultiplexer #(.width(7)) demultiplexer_3 (
    .out1(demultiplexer_3_out1), .in(7'b1100101), .sel(xor_4_out));  // open: out0
  Multiplexer #(.width(7)) multiplexer_2 (
    .in0(7'b1110010), .in1({7{1'b0}}), .out(multiplexer_2_out), .sel(xor_2_out[2]));
  Multiplexer #(.width(7)) multiplexer_3 (
    .in0({xor_2_out[7:3], xor_2_out[1:0]}), .in1(and_3_out), .out(multiplexer_3_out), .sel(not_3_out));
  not not_3 (not_3_out, comparator_1_eq);
  assign and_5_out = 7'b1100001 & {7{xor_3_out[7]}};  // AND_Gate and_5, 7 bits wide
  Verifier verifier_1 (
    .P1(multiplexer_1_out), .P2(demultiplexer_2_out1), .P3(multiplexer_2_out), .P4(demultiplexer_3_out1),
    .P5(multiplexer_3_out), .P6(and_5_out), .P7(7'b0100001), .P8(7'b0100001), .C(C), .R(in_1),
    .O(verifier_1_o), .D(verifier_1_d));
  TTY tty_1 (.data(verifier_1_o), .clk(C), .we(verifier_1_d), .clr(in_1));

  // Other names for the same wires on the sheet: R = in_1

  // Notes on the sheet:
  //   Flag
  //   Do not Modify the circuit
  //   Understand it and try to find the correct flag which redirects all the nonzero constants to the verifier
endmodule

module Verifier (
  input  [6:0] P1,
  input  [6:0] P2,
  input  [6:0] P3,
  input  [6:0] P4,
  input  [6:0] P5,
  input  [6:0] P6,
  input  [6:0] P7,
  input  [6:0] P8,
  input  C,
  input  R,
  output [6:0] O,
  output D
);

  wire and_1_out;
  wire [2:0] adder_1_out, multiplexer_2_out, register_1_q;

  Multiplexer #(.select(3), .width(7)) multiplexer_1 (
    .in0(P1), .in1(P2), .in2(P3), .in3(P4), .in4(P5), .in5(P6), .in6(P7), .in7(P8), .out(O),
    .sel(register_1_q));
  Adder #(.width(3)) adder_1 (.a(3'b001), .b(register_1_q), .out(adder_1_out));  // open: cin, cout
  Multiplexer #(.width(3)) multiplexer_2 (.in0(adder_1_out), .in1(3'b111), .out(multiplexer_2_out), .sel(and_1_out));
  and and_1 (and_1_out, register_1_q[0], register_1_q[1], register_1_q[2]);
  Register #(.width(3)) register_1 (.D(multiplexer_2_out), .en(1'b1), .clk(C), .Q(register_1_q), .clr(R));
  // Probe on O
  D_Flip_Flop d_ff_1 (.D(and_1_out), .clk(C), .Qn(D));  // open: Q, preset, reset
endmodule
