// Logisim project What_the_hell.circ as structural Verilog: 2 circuits, main circuit main
module main (
  input  reset
);

  wire clk_out, verifier_1_res;
  wire [2:0] undriven;

  Clock clk (.out(clk_out));
  Verifier verifier_1 (.test(undriven), .clk(clk_out), .rst(reset), .res(verifier_1_res));
  LED led_1 (.in(verifier_1_res));

  // Notes on the sheet:
  //   Implement your counter here
  //   If you implement the counter correctly then the LED should be lit for all the clock cycles
endmodule

module Verifier (
  input  [2:0] test,
  input  clk,
  input  rst,
  output res
);

  wire and_1_out, and_2_out, and_3_out, and_4_out, and_5_out, and_6_out, and_7_out, and_8_out, not_1_out,
       not_2_out, or_1_out, or_2_out;
  wire [2:0] counter_1_q;

  and and_1 (and_1_out, test[0], test[1]);
  not not_1 (not_1_out, and_1_out);
  and and_2 (and_2_out, test[0], test[1], test[2]);
  not not_2 (not_2_out, and_2_out);
  and and_3 (and_3_out, test[0], test[1]);
  and and_4 (and_4_out, and_3_out, ~test[2]);  // AND_Gate
  and and_5 (and_5_out, ~test[0], test[1], ~test[2]);  // AND_Gate
  or or_1 (or_1_out, test[0], ~test[1], test[2]);  // OR_Gate
  or or_2 (or_2_out, ~test[0], ~test[1], test[2]);  // OR_Gate
  and and_6 (and_6_out, test[0], test[1], test[2]);
  and and_7 (and_7_out, ~test[0], test[1], test[2]);  // AND_Gate
  and and_8 (and_8_out, not_1_out, test[2]);
  Counter #(.max('h7), .width(3)) counter_1 (
    .count(1'b1), .Q(counter_1_q), .up(1'b1), .clk(clk), .clr(rst));  // open: load, D, carry
  Multiplexer #(.select(3)) multiplexer_1 (
    .in0(and_8_out), .in1(not_2_out), .in2(and_4_out), .in3(and_5_out), .in4(or_1_out), .in5(or_2_out),
    .in6(and_6_out), .in7(and_7_out), .out(res), .sel(counter_1_q));

  // Notes on the sheet:
  //   DO NOT MODIFY THIS!!
endmodule
